# Fritzing sketch fritzing (saved by Fritzing 0.9.3b)
breadboards: 1

parts:
  WeMos_D1_Mini1 = WeMos D1 Mini
  MQ-135 = female pin header, 4 pins [form="♀ (female)"]
  SDS-011 = female alternating pin header, 7 pins [form="♀ (female)"]
  Grove3 = TM1637 4 Digit Display
  Grove1 = TM1637 4 Digit Display
  Grove2 = TM1637 4 Digit Display

nets:
  VCC: WeMos_D1_Mini1.5V, MQ-135.pin4, SDS-011.pin4, SDS-011.pin5, Grove3.VCC, Grove1.VCC, Grove2.VCC
  N1: WeMos_D1_Mini1.A0, MQ-135.pin1
  N2: WeMos_D1_Mini1.D0, Grove2.CLK
  N3: WeMos_D1_Mini1.D1, Grove3.CLK
  N4: WeMos_D1_Mini1.D2, Grove3.DIO
  N5: WeMos_D1_Mini1.D3, Grove1.CLK
  N6: WeMos_D1_Mini1.D4, Grove1.DIO
  N7: WeMos_D1_Mini1.D5, Grove2.DIO
  N8: WeMos_D1_Mini1.D6, SDS-011.pin1
  N9: WeMos_D1_Mini1.D7, SDS-011.pin2
  GND: WeMos_D1_Mini1.G, MQ-135.pin3, SDS-011.pin3, Grove3.GND, Grove1.GND, Grove2.GND

notes:
  A0
  GND
  VCC
  TX
  RX
  5V

custom parts:
  WeMos D1 Mini: The D1 mini is a mini wifi board based on ESP-8266EX.
  TM1637 4 Digit Display: A 4 7-seg display, modeled from a RobotDyn TM1637 display
